// Logisim project RISC.circ as structural Verilog
module adder (
  input  in_1,
  input  in_2,
  output out_3,
  output out_4
);

  and and_1 (out_3, in_1, in_2);
  xor xor_1 (out_4, in_1, in_2);
endmodule

module fulladder (
  input  in_1,
  input  in_2,
  input  in_3,
  output \进位 ,
  output \输出 
);

  wire adder_1_out_3, adder_1_out_4, adder_2_out_3;

  adder adder_1 (.in_1(in_1), .in_2(in_2), .out_3(adder_1_out_3), .out_4(adder_1_out_4));
  adder adder_2 (.in_1(adder_1_out_4), .in_2(in_3), .out_3(adder_2_out_3), .out_4(\输出 ));
  or or_1 (\进位 , adder_1_out_3, adder_2_out_3);

  // Notes on the sheet:
  //   两个输入加数
  //   上一个进位
endmodule

module _4bitadder (
  input  in_1,
  input  in_2,
  input  in_3,
  input  in_4,
  input  in_5,
  input  in_6,
  input  in_7,
  input  in_8,
  input  in_9,
  output out_10,
  output out_11,
  output out_12,
  output out_13,
  output out_14
);

  wire \fulladder_1_进位 , \fulladder_2_进位 , \fulladder_3_进位 ;

  fulladder fulladder_1 (.in_1(in_1), .in_2(in_5), .in_3(in_9), .\进位 (\fulladder_1_进位 ), .\输出 (out_14));
  fulladder fulladder_2 (.in_1(in_3), .in_2(in_7), .in_3(\fulladder_3_进位 ), .\进位 (\fulladder_2_进位 ), .\输出 (out_12));
  fulladder fulladder_3 (.in_1(in_2), .in_2(in_6), .in_3(\fulladder_1_进位 ), .\进位 (\fulladder_3_进位 ), .\输出 (out_13));
  fulladder fulladder_4 (.in_1(in_4), .in_2(in_8), .in_3(\fulladder_2_进位 ), .\进位 (out_10), .\输出 (out_11));
endmodule

module \减法器  (
  input  in_1,
  input  in_2,
  input  in_3,
  input  in_4,
  input  in_5,
  input  in_6,
  input  in_7,
  input  in_8,
  output out_9,
  output out_10,
  output \输出 ,
  output out_12,
  output out_13
);

  wire not_1_out, not_2_out, not_3_out, not_4_out;

  not not_1 (not_1_out, in_5);
  not not_2 (not_2_out, in_6);
  not not_3 (not_3_out, in_7);
  not not_4 (not_4_out, in_8);
  _4bitadder u_4bitadder_1 (
    .in_1(in_1), .in_2(in_2), .in_3(in_3), .in_4(in_4), .in_5(not_1_out), .in_6(not_2_out), .in_7(not_3_out),
    .in_8(not_4_out), .in_9(1'b1), .out_10(out_9), .out_11(out_10), .out_12(\输出 ), .out_13(out_12),
    .out_14(out_13));

  // Notes on the sheet:
  //   被减数
  //   减数
endmodule

module ALU (
  input  [3:0] \被减数 ,
  input  [3:0] \减数 ,
  input  in_3,
  input  in_4,
  input  \使能 ,
  output out_6,
  output out_7,
  output out_8,
  output out_9,
  output out_10
);

  wire multiplexer_2_out;
  wire [3:0] multiplexer_1_out, not_1_out;

  Multiplexer #(.width(4)) multiplexer_1 (.in0(\减数 ), .in1(not_1_out), .out(multiplexer_1_out), .sel(in_4), .en(\使能 ));
  assign not_1_out = ~\减数 ;  // NOT_Gate not_1, 4 bits wide
  Multiplexer multiplexer_2 (.in0(in_3), .in1(1'b1), .out(multiplexer_2_out), .sel(in_4), .en(\使能 ));
  _4bitadder u_4bitadder_1 (
    .in_1(\被减数 [0]), .in_2(\被减数 [1]), .in_3(\被减数 [2]), .in_4(\被减数 [3]), .in_5(multiplexer_1_out[0]),
    .in_6(multiplexer_1_out[1]), .in_7(multiplexer_1_out[2]), .in_8(multiplexer_1_out[3]),
    .in_9(multiplexer_2_out), .out_10(out_6), .out_11(out_7), .out_12(out_8), .out_13(out_9), .out_14(out_10));

  // Notes on the sheet:
  //   0加法，1减法
endmodule

module \寄存器组  (
  input  in_1,
  input  in_2,
  input  \被减数 ,
  input  in_4,
  input  in_5,
  input  in_6,
  input  in_7,
  input  in_8,
  input  in_9,
  input  in_10,
  input  in_11,
  input  in_12,
  input  in_13,
  input  in_14,
  input  in_15,
  input  in_16,
  input  [1:0] \数据选择 ,
  input  [3:0] in_18,
  input  in_19,
  input  in_20,
  input  in_21,
  output out_22,
  output out_23,
  output out_24,
  output out_25,
  output out_26,
  output out_27,
  output out_28,
  output out_29,
  output out_30,
  output out_31,
  output _3,
  output out_33,
  output out_34,
  output _1,
  output out_36,
  output out_37,
  output out_38,
  output out_39,
  output out_40,
  output out_41,
  output out_42
);

  wire clock_1_out, clock_2_out, clock_3_out, clock_4_out;
  wire [3:0] multiplexer_1_out;

  Clock clock_1 (.out(clock_1_out));
  Clock clock_2 (.out(clock_2_out));
  D_Flip_Flop d_ff_1 (.clk(clock_1_out), .D(in_1), .Q(out_22));  // open: Qn, preset, en, reset
  D_Flip_Flop d_ff_2 (.clk(clock_1_out), .D(\被减数 ), .Q(out_24));  // open: Qn, preset, en, reset
  D_Flip_Flop d_ff_3 (.clk(clock_1_out), .D(in_5), .Q(out_26));  // open: Qn, preset, en, reset
  D_Flip_Flop d_ff_4 (.clk(clock_1_out), .D(in_7), .Q(out_28));  // open: Qn, preset, en, reset
  D_Flip_Flop d_ff_5 (.clk(clock_2_out), .D(in_9), .Q(out_30));  // open: Qn, preset, en, reset
  D_Flip_Flop d_ff_6 (.clk(clock_2_out), .D(in_11), .Q(_3));  // open: Qn, preset, en, reset
  D_Flip_Flop d_ff_7 (.clk(clock_2_out), .D(in_13), .Q(out_34));  // open: Qn, preset, en, reset
  D_Flip_Flop d_ff_8 (.clk(clock_2_out), .D(in_15), .Q(out_36));  // open: Qn, preset, en, reset
  Clock clock_3 (.out(clock_3_out));
  Clock clock_4 (.out(clock_4_out));
  D_Flip_Flop d_ff_9 (.clk(clock_3_out), .D(in_2), .Q(out_23));  // open: Qn, preset, en, reset
  D_Flip_Flop d_ff_10 (.clk(clock_3_out), .D(in_4), .Q(out_25));  // open: Qn, preset, en, reset
  D_Flip_Flop d_ff_11 (.clk(clock_3_out), .D(in_6), .Q(out_27));  // open: Qn, preset, en, reset
  D_Flip_Flop d_ff_12 (.clk(clock_3_out), .D(in_8), .Q(out_29));  // open: Qn, preset, en, reset
  D_Flip_Flop d_ff_13 (.clk(clock_4_out), .D(in_10), .Q(out_31));  // open: Qn, preset, en, reset
  D_Flip_Flop d_ff_14 (.clk(clock_4_out), .D(in_12), .Q(out_33));  // open: Qn, preset, en, reset
  D_Flip_Flop d_ff_15 (.clk(clock_4_out), .D(in_14), .Q(_1));  // open: Qn, preset, en, reset
  D_Flip_Flop d_ff_16 (.clk(clock_4_out), .D(in_16), .Q(out_37));  // open: Qn, preset, en, reset
  Multiplexer #(.select(2), .width(4), .enable("false")) multiplexer_1 (
    .in0({out_23, out_25, out_27, out_29}), .in1({out_31, out_33, _1, out_37}),
    .in2({out_22, out_24, out_26, out_28}), .in3({out_30, _3, out_34, out_36}), .out(multiplexer_1_out),
    .sel(\数据选择 ));
  ALU alu_1 (
    .\被减数 (multiplexer_1_out), .\减数 (in_18), .in_3(in_19), .in_4(in_20), .\使能 (in_21), .out_6(out_38),
    .out_7(out_39), .out_8(out_40), .out_9(out_41), .out_10(out_42));

  // Notes on the sheet:
  //   减数
  //   2
  //   0
  //   加法的上一级进位
  //   0加法1减法
  //   1使能
endmodule

module \_4个寄存器  (
  input  in_1,
  input  in_2,
  input  in_3,
  input  in_4,
  input  in_5,
  output out_6,
  output out_7,
  output out_8,
  output out_9
);

  D_Flip_Flop d_ff_1 (.clk(in_1), .D(in_2), .Q(out_6));  // open: Qn, preset, en, reset
  D_Flip_Flop d_ff_2 (.clk(in_1), .D(in_3), .Q(out_7));  // open: Qn, preset, en, reset
  D_Flip_Flop d_ff_3 (.clk(in_1), .D(in_4), .Q(out_8));  // open: Qn, preset, en, reset
  D_Flip_Flop d_ff_4 (.clk(in_1), .D(in_5), .Q(out_9));  // open: Qn, preset, en, reset
endmodule

module \第一版CPU  (
  input  [3:0] in_1,
  input  [3:0] in_2,
  input  [3:0] in_3,
  input  [3:0] in_4,
  input  in_5,
  input  [2:0] in_6,
  input  in_7,
  input  [1:0] in_8,
  input  [1:0] in_9,
  output [3:0] out_10,
  output [3:0] out_11,
  output [3:0] out_12,
  output [3:0] _1
);

  wire alu_1_out_6, clock_1_out, clock_2_out, clock_3_out, clock_4_out, clock_5_out, clock_6_out,
       clock_7_out, clock_8_out;
  wire [3:0] alu_1_out_10, multiplexer_1_out, multiplexer_2_out, \n4个寄存器_1_out_9 , \n4个寄存器_2_out_9 ,
       \n4个寄存器_5_out_9 , \n4个寄存器_6_out_9 , \寄存器0 , \寄存器1 , \寄存器2 , \寄存器3 ;

  Clock clock_1 (.out(clock_1_out));
  Clock clock_2 (.out(clock_2_out));
  Clock clock_3 (.out(clock_3_out));
  Clock clock_4 (.out(clock_4_out));
  \_4个寄存器  \u_4个寄存器_1  (
    .in_1(clock_1_out), .in_2(in_1[3]), .in_3(in_1[2]), .in_4(in_1[1]), .in_5(in_1[0]),
    .out_6(\n4个寄存器_1_out_9 [3]), .out_7(\n4个寄存器_1_out_9 [2]), .out_8(\n4个寄存器_1_out_9 [1]),
    .out_9(\n4个寄存器_1_out_9 [0]));
  \_4个寄存器  \u_4个寄存器_2  (
    .in_1(clock_2_out), .in_2(in_3[3]), .in_3(in_3[2]), .in_4(in_3[1]), .in_5(in_3[0]),
    .out_6(\n4个寄存器_2_out_9 [3]), .out_7(\n4个寄存器_2_out_9 [2]), .out_8(\n4个寄存器_2_out_9 [1]),
    .out_9(\n4个寄存器_2_out_9 [0]));
  \_4个寄存器  \u_4个寄存器_3  (
    .in_1(clock_3_out), .in_2(\寄存器2 [3]), .in_3(\寄存器2 [2]), .in_4(\寄存器2 [1]), .in_5(\寄存器2 [0]),
    .out_6(out_12[3]), .out_7(out_12[2]), .out_8(out_12[1]), .out_9(out_12[0]));
  \_4个寄存器  \u_4个寄存器_4  (
    .in_1(clock_4_out), .in_2(\寄存器3 [3]), .in_3(\寄存器3 [2]), .in_4(\寄存器3 [1]), .in_5(\寄存器3 [0]),
    .out_6(out_11[3]), .out_7(out_11[2]), .out_8(out_11[1]), .out_9(out_11[0]));
  Clock clock_5 (.out(clock_5_out));
  Clock clock_6 (.out(clock_6_out));
  Clock clock_7 (.out(clock_7_out));
  Clock clock_8 (.out(clock_8_out));
  \_4个寄存器  \u_4个寄存器_5  (
    .in_1(clock_6_out), .in_2(in_2[3]), .in_3(in_2[2]), .in_4(in_2[1]), .in_5(in_2[0]),
    .out_6(\n4个寄存器_5_out_9 [3]), .out_7(\n4个寄存器_5_out_9 [2]), .out_8(\n4个寄存器_5_out_9 [1]),
    .out_9(\n4个寄存器_5_out_9 [0]));
  \_4个寄存器  \u_4个寄存器_6  (
    .in_1(clock_7_out), .in_2(in_4[3]), .in_3(in_4[2]), .in_4(in_4[1]), .in_5(in_4[0]),
    .out_6(\n4个寄存器_6_out_9 [3]), .out_7(\n4个寄存器_6_out_9 [2]), .out_8(\n4个寄存器_6_out_9 [1]),
    .out_9(\n4个寄存器_6_out_9 [0]));
  \_4个寄存器  \u_4个寄存器_7  (
    .in_1(clock_8_out), .in_2(\寄存器0 [3]), .in_3(\寄存器0 [2]), .in_4(\寄存器0 [1]), .in_5(\寄存器0 [0]),
    .out_6(out_10[3]), .out_7(out_10[2]), .out_8(out_10[1]), .out_9(out_10[0]));
  \_4个寄存器  \u_4个寄存器_8  (
    .in_1(clock_5_out), .in_2(\寄存器1 [3]), .in_3(\寄存器1 [2]), .in_4(\寄存器1 [1]), .in_5(\寄存器1 [0]),
    .out_6(_1[3]), .out_7(_1[2]), .out_8(_1[1]), .out_9(_1[0]));
  Multiplexer #(.select(2), .width(4), .enable("false")) multiplexer_1 (
    .in0(\n4个寄存器_5_out_9 ), .in1(\n4个寄存器_6_out_9 ), .in2(\n4个寄存器_1_out_9 ), .in3(\n4个寄存器_2_out_9 ),
    .out(multiplexer_1_out), .sel(in_9));
  Multiplexer #(.select(2), .width(4), .enable("false")) multiplexer_2 (
    .in0(out_10), .in1(_1), .in2(out_12), .in3(out_11), .out(multiplexer_2_out), .sel(in_8));
  ALU alu_1 (
    .\被减数 (multiplexer_2_out), .\减数 (multiplexer_1_out), .in_3(in_5), .in_4(in_7), .\使能 (1'b1),
    .out_6(alu_1_out_6), .out_7(alu_1_out_10[3]), .out_8(alu_1_out_10[2]), .out_9(alu_1_out_10[1]),
    .out_10(alu_1_out_10[0]));
  Demultiplexer #(.select(2), .width(4), .tristate("true"), .enable("false")) demultiplexer_1 (
    .out0(\寄存器0 ), .out1(\寄存器1 ), .out2(\寄存器2 ), .out3(\寄存器3 ), .in(alu_1_out_10), .sel(in_8));

  // Notes on the sheet:
  //   2
  //   3
  //   2
  //   3
  //   0
  //   1
  //   加法的上一级进位
  //   0加法1减法
  //   1使能
  //   0
  //   数据选择
  //   数据选择
endmodule

module \存储器2  (
  input  [7:0] in_1,
  input  [1:0] in_2,
  input  in_3,
  input  in_4,
  input  [1:0] in_5,
  input  [1:0] in_6,
  output [7:0] out_7
);

  wire clock_1_out, decoder_1_out0, not_1_out;
  wire [7:0] ram_1_data;

  Clock clock_1 (.out(clock_1_out));
  Decoder #(.enable("false")) decoder_1 (.out0(decoder_1_out0), .sel(in_4));  // open: out1
  RAM #(.addrWidth(2)) ram_1 (
    .addr(in_5), .data(ram_1_data), .clk(clock_1_out), .ld(decoder_1_out0));  // open: sel, clr
  not not_1 (not_1_out, decoder_1_out0);
  assign ram_1_data = not_1_out ? in_1 : 8'bz;  // Controlled_Buffer controlled_buffer_1
  assign out_7 = decoder_1_out0 ? ram_1_data : 8'bz;  // Controlled_Buffer controlled_buffer_2
endmodule

module \第二版CPU  (
  input  \数据选择 ,
  input  [3:0] in_2,
  input  [1:0] in_3,
  input  [1:0] in_4,
  output [3:0] out_5
);

  wire alu_1_out_6, clock_1_out, clock_2_out, clock_3_out, clock_4_out, clock_5_out, not_1_out, or_1_out,
       or_2_out, \减法指令 , \加法指令 , \加载指令 , \存储指令 ;
  wire [3:0] _0, _1, _2, _3, alu_1_out_10, multiplexer_1_out, multiplexer_2_out, \寄存器0 , \寄存器1 , \寄存器2 ,
       \寄存器3 ;

  Clock clock_1 (.out(clock_1_out));
  Clock clock_2 (.out(clock_2_out));
  Decoder #(.select(4), .disabled(0), .enable("false")) decoder_1 (
    .out0(\加法指令 ), .out1(\减法指令 ), .out2(\加载指令 ), .out3(\存储指令 ), .sel(in_2));  // open: out4, out5, out6, out7, out8, out9, out10, out11, out12, out13, out14, out15
  \_4个寄存器  \u_4个寄存器_1  (
    .in_1(clock_1_out), .in_2(\寄存器2 [3]), .in_3(\寄存器2 [2]), .in_4(\寄存器2 [1]), .in_5(\寄存器2 [0]),
    .out_6(_2[3]), .out_7(_2[2]), .out_8(_2[1]), .out_9(_2[0]));
  \_4个寄存器  \u_4个寄存器_2  (
    .in_1(clock_2_out), .in_2(\寄存器3 [3]), .in_3(\寄存器3 [2]), .in_4(\寄存器3 [1]), .in_5(\寄存器3 [0]),
    .out_6(_3[3]), .out_7(_3[2]), .out_8(_3[1]), .out_9(_3[0]));
  or or_1 (or_1_out, \存储指令 , \加载指令 );
  Clock clock_3 (.out(clock_3_out));
  Clock clock_4 (.out(clock_4_out));
  Clock clock_5 (.out(clock_5_out));
  \_4个寄存器  \u_4个寄存器_3  (
    .in_1(clock_4_out), .in_2(\寄存器0 [3]), .in_3(\寄存器0 [2]), .in_4(\寄存器0 [1]), .in_5(\寄存器0 [0]),
    .out_6(_0[3]), .out_7(_0[2]), .out_8(_0[1]), .out_9(_0[0]));
  \_4个寄存器  \u_4个寄存器_4  (
    .in_1(clock_5_out), .in_2(\寄存器1 [3]), .in_3(\寄存器1 [2]), .in_4(\寄存器1 [1]), .in_5(\寄存器1 [0]),
    .out_6(_1[3]), .out_7(_1[2]), .out_8(_1[1]), .out_9(_1[0]));
  Multiplexer #(.select(2), .width(4), .enable("false")) multiplexer_1 (
    .in0(_0), .in1(_1), .in2(_2), .in3(_3), .out(multiplexer_1_out), .sel(in_4));
  or or_2 (or_2_out, \加法指令 , \减法指令 );
  RAM #(.addrWidth(2), .dataWidth(4)) ram_1 (
    .addr(in_4), .data(out_5), .sel(or_1_out), .clk(clock_3_out), .ld(\加载指令 ));  // open: clr
  Multiplexer #(.select(2), .width(4), .enable("false")) multiplexer_2 (
    .in0(_0), .in1(_1), .in2(_2), .in3(_3), .out(multiplexer_2_out), .sel(in_3));
  Multiplexer #(.select(2), .width(4)) multiplexer_3 (
    .in0(_0), .in1(_1), .in2(_2), .in3(_3), .out(out_5), .sel(in_3), .en(not_1_out));
  not not_1 (not_1_out, \加载指令 );
  ALU alu_1 (
    .\被减数 (multiplexer_2_out), .\减数 (multiplexer_1_out), .in_3(\数据选择 ), .in_4(\减法指令 ), .\使能 (or_2_out),
    .out_6(alu_1_out_6), .out_7(alu_1_out_10[3]), .out_8(alu_1_out_10[2]), .out_9(alu_1_out_10[1]),
    .out_10(alu_1_out_10[0]));
  Demultiplexer #(.select(2), .width(4), .tristate("true")) demultiplexer_1 (
    .out0(\寄存器0 ), .out1(\寄存器1 ), .out2(\寄存器2 ), .out3(\寄存器3 ), .in(alu_1_out_10), .sel(in_3), .en(or_2_out));
  Demultiplexer #(.select(2), .width(4), .tristate("true")) demultiplexer_2 (
    .out0(\寄存器0 ), .out1(\寄存器1 ), .out2(\寄存器2 ), .out3(\寄存器3 ), .in(out_5), .sel(in_3), .en(\加载指令 ));

  // Other names for the same wires on the sheet: Rd[1:0] = in_3; Rs[1:0] = in_4

  // Notes on the sheet:
  //   指令见指令结构
  //   存储器
  //   2
  //   3
  //   加法的上一级进位
  //   0加法1减法
  //   1使能
  //   数据选择
  //   0
  //   数据选择
  //   运算单元
endmodule

module \存储器  (
  input  [7:0] in_1,
  input  [7:0] in_2,
  input  in_3,
  input  in_4,
  output [7:0] out_5
);

  wire not_1_out, \时钟 ;
  wire [3:0] ram_1_data, ram_2_data;

  Clock #(.highDuration(3), .lowDuration(3)) clock_1 (.out(\时钟 ));
  RAM #(.dataWidth(4)) ram_1 (.addr(in_2), .data(ram_1_data), .sel(in_3), .clk(\时钟 ), .ld(in_4));  // open: clr
  RAM #(.dataWidth(4)) ram_2 (.addr(in_2), .data(ram_2_data), .sel(in_3), .clk(\时钟 ), .ld(in_4));  // open: clr
  not not_1 (not_1_out, in_4);
  assign {ram_2_data, ram_1_data} = not_1_out ? in_1 : 8'bz;  // Controlled_Buffer controlled_buffer_1
  assign out_5 = in_4 ? {ram_2_data, ram_1_data} : 8'bz;  // Controlled_Buffer controlled_buffer_2

  // Other names for the same wires on the sheet: _0写1读 = in_4; 使能 = in_3; 地址[7:0] = in_2

  // Notes on the sheet:
  //   低8位
  //   高8位
  //   写
  //   读
endmodule

module \存储器字扩展  (
  input  [7:0] in_1,
  input  in_2,
  input  [7:0] in_3,
  input  in_4,
  output [7:0] out_5
);

  wire not_1_out, not_2_out, \时钟 ;
  wire [7:0] ram_1_data;

  not not_1 (not_1_out, in_2);
  RAM ram_1 (.addr(in_3), .data(ram_1_data), .sel(in_2), .clk(\时钟 ), .ld(in_4));  // open: clr
  RAM ram_2 (.addr(in_3), .data(ram_1_data), .sel(not_1_out), .clk(\时钟 ), .ld(in_4));  // open: clr
  not not_2 (not_2_out, in_4);
  assign ram_1_data = not_2_out ? in_1 : 8'bz;  // Controlled_Buffer controlled_buffer_1
  assign out_5 = in_4 ? ram_1_data : 8'bz;  // Controlled_Buffer controlled_buffer_2
  Clock #(.highDuration(3), .lowDuration(3)) clock_1 (.out(\时钟 ));

  // Other names for the same wires on the sheet: _0写1读 = in_4; 使能 = in_2; 地址[7:0] = in_3

  // Notes on the sheet:
  //   高8位
  //   低8位
  //   写
  //   读
endmodule

module \_3_8译码器  (
  input  in_1,
  input  [15:0] in_2,
  input  [7:0] \存储 ,
  output [7:0] \读取 
);

  wire \_1号 , \_2号 , \_3号 , \_4号 , \_5号 , \_6号 , \_7号 , \_8号 , not_1_out, not_2_out, not_3_out, not_4_out,
       not_5_out, not_6_out, not_7_out, not_8_out, not_9_out, not_10_out, not_11_out, not_12_out, not_13_out,
       not_14_out, not_15_out, not_16_out, \时钟 , \清零 ;

  Decoder #(.select(3)) decoder_1 (
    .out0(\_1号 ), .out1(\_2号 ), .out2(\_3号 ), .out3(\_4号 ), .out4(\_5号 ), .out5(\_6号 ), .out6(\_7号 ),
    .out7(\_8号 ), .sel(in_2[2:0]), .en(in_2[13]));
  not not_1 (not_1_out, in_1);
  not not_2 (not_2_out, in_1);
  not not_3 (not_3_out, in_1);
  not not_4 (not_4_out, in_1);
  RAM #(.dataWidth(4), .bus("separate")) ram_1 (
    .addr(in_2[10:3]), .din(\存储 [3:0]), .data(\读取 [3:0]), .str(not_1_out), .sel(\_1号 ), .clk(\时钟 ),
    .ld(in_1), .clr(\清零 ));
  RAM #(.dataWidth(4), .bus("separate")) ram_2 (
    .addr(in_2[10:3]), .din(\存储 [7:4]), .data(\读取 [7:4]), .str(not_2_out), .sel(\_1号 ), .clk(\时钟 ),
    .ld(in_1), .clr(\清零 ));
  RAM #(.dataWidth(4), .bus("separate")) ram_3 (
    .addr(in_2[10:3]), .din(\存储 [3:0]), .data(\读取 [3:0]), .str(not_3_out), .sel(\_5号 ), .clk(\时钟 ),
    .ld(in_1), .clr(\清零 ));
  RAM #(.dataWidth(4), .bus("separate")) ram_4 (
    .addr(in_2[10:3]), .din(\存储 [7:4]), .data(\读取 [7:4]), .str(not_4_out), .sel(\_5号 ), .clk(\时钟 ),
    .ld(in_1), .clr(\清零 ));
  Clock #(.highDuration(5), .lowDuration(5)) clock_1 (.out(\时钟 ));
  not not_5 (not_5_out, in_1);
  not not_6 (not_6_out, in_1);
  not not_7 (not_7_out, in_1);
  not not_8 (not_8_out, in_1);
  RAM #(.dataWidth(4), .bus("separate")) ram_5 (
    .addr(in_2[10:3]), .din(\存储 [3:0]), .data(\读取 [3:0]), .str(not_5_out), .sel(\_2号 ), .clk(\时钟 ),
    .ld(in_1), .clr(\清零 ));
  RAM #(.dataWidth(4), .bus("separate")) ram_6 (
    .addr(in_2[10:3]), .din(\存储 [7:4]), .data(\读取 [7:4]), .str(not_6_out), .sel(\_2号 ), .clk(\时钟 ),
    .ld(in_1), .clr(\清零 ));
  RAM #(.dataWidth(4), .bus("separate")) ram_7 (
    .addr(in_2[10:3]), .din(\存储 [3:0]), .data(\读取 [3:0]), .str(not_7_out), .sel(\_6号 ), .clk(\时钟 ),
    .ld(in_1), .clr(\清零 ));
  RAM #(.dataWidth(4), .bus("separate")) ram_8 (
    .addr(in_2[10:3]), .din(\存储 [7:4]), .data(\读取 [7:4]), .str(not_8_out), .sel(\_6号 ), .clk(\时钟 ),
    .ld(in_1), .clr(\清零 ));
  not not_9 (not_9_out, in_1);
  not not_10 (not_10_out, in_1);
  not not_11 (not_11_out, in_1);
  not not_12 (not_12_out, in_1);
  RAM #(.dataWidth(4), .bus("separate")) ram_9 (
    .addr(in_2[10:3]), .din(\存储 [3:0]), .data(\读取 [3:0]), .str(not_9_out), .sel(\_3号 ), .clk(\时钟 ),
    .ld(in_1), .clr(\清零 ));
  RAM #(.dataWidth(4), .bus("separate")) ram_10 (
    .addr(in_2[10:3]), .din(\存储 [7:4]), .data(\读取 [7:4]), .str(not_10_out), .sel(\_3号 ), .clk(\时钟 ),
    .ld(in_1), .clr(\清零 ));
  RAM #(.dataWidth(4), .bus("separate")) ram_11 (
    .addr(in_2[10:3]), .din(\存储 [3:0]), .data(\读取 [3:0]), .str(not_11_out), .sel(\_7号 ), .clk(\时钟 ),
    .ld(in_1), .clr(\清零 ));
  RAM #(.dataWidth(4), .bus("separate")) ram_12 (
    .addr(in_2[10:3]), .din(\存储 [7:4]), .data(\读取 [7:4]), .str(not_12_out), .sel(\_7号 ), .clk(\时钟 ),
    .ld(in_1), .clr(\清零 ));
  not not_13 (not_13_out, in_1);
  not not_14 (not_14_out, in_1);
  not not_15 (not_15_out, in_1);
  not not_16 (not_16_out, in_1);
  RAM #(.dataWidth(4), .bus("separate")) ram_13 (
    .addr(in_2[10:3]), .din(\存储 [3:0]), .data(\读取 [3:0]), .str(not_13_out), .sel(\_4号 ), .clk(\时钟 ),
    .ld(in_1), .clr(\清零 ));
  RAM #(.dataWidth(4), .bus("separate")) ram_14 (
    .addr(in_2[10:3]), .din(\存储 [7:4]), .data(\读取 [7:4]), .str(not_14_out), .sel(\_4号 ), .clk(\时钟 ),
    .ld(in_1), .clr(\清零 ));
  RAM #(.dataWidth(4), .bus("separate")) ram_15 (
    .addr(in_2[10:3]), .din(\存储 [3:0]), .data(\读取 [3:0]), .str(not_15_out), .sel(\_8号 ), .clk(\时钟 ),
    .ld(in_1), .clr(\清零 ));
  RAM #(.dataWidth(4), .bus("separate")) ram_16 (
    .addr(in_2[10:3]), .din(\存储 [7:4]), .data(\读取 [7:4]), .str(not_16_out), .sel(\_8号 ), .clk(\时钟 ),
    .ld(in_1), .clr(\清零 ));

  // Other names for the same wires on the sheet: 地址[10:0] = in_2[10:0]; _0写1读 = in_1; _1使能 = in_2[13];
  //   存储数据前4位[3:0] = \存储 [3:0]; 存储数据后4位[3:0] = \存储 [7:4]; 读取数据前4位[3:0] = \读取 [3:0]; 读取数据后4位[3:0] = \读取 [7:4]

  // Notes on the sheet:
  //   位扩展和字扩展
  //   0x2000-0x20FF
  //   0x2100-0x21FF
  //   0x2200-0x22FF
  //   0x2300-0x23FF
  //   0x2400-0x24FF
  //   0x2500-0x25FF
  //   0x2600-0x26FF
  //   0x2700-0x27FF
  //   地址高位在前
  //   总地址范围：0x2000-0x27FF
endmodule

module \第2版运算单元  (
  input  in_1,
  input  [7:0] in_2,
  input  [7:0] in_3,
  output [7:0] out_4,
  output out_5
);

  Adder adder_1 (.a(in_2), .b(in_3), .out(out_4), .cin(in_1), .cout(out_5));
endmodule

module \第二版运算单元  (
  input  in_1,
  input  [7:0] in_2,
  input  [7:0] in_3,
  input  in_4,
  input  in_5,
  output [7:0] out_6,
  output out_7
);

  wire multiplexer_1_out;
  wire [7:0] multiplexer_2_out, not_1_out;

  assign not_1_out = ~in_3;  // NOT_Gate not_1, 8 bits wide
  Multiplexer multiplexer_1 (.in0(in_1), .in1(1'b1), .out(multiplexer_1_out), .sel(in_4), .en(in_5));
  Multiplexer #(.width(8)) multiplexer_2 (.in0(in_3), .in1(not_1_out), .out(multiplexer_2_out), .sel(in_4), .en(in_5));
  \第2版运算单元  \u_第2版运算单元_1  (
    .in_1(multiplexer_1_out), .in_2(in_2), .in_3(multiplexer_2_out), .out_4(out_6), .out_5(out_7));

  // Other names for the same wires on the sheet: _0加法1减法 = in_4; 使能 = in_5
endmodule

module \寄存器  (
  input  [2:0] \地址 ,
  input  [7:0] \数据输入 ,
  input  in_3,
  input  in_4,
  input  in_5,
  input  in_6,
  output [7:0] \数据输出 
);

  wire not_1_out;

  not not_1 (not_1_out, in_3);
  RAM #(.addrWidth(3), .bus("separate")) ram_1 (
    .addr(\地址 ), .din(\数据输入 ), .data(\数据输出 ), .str(not_1_out), .sel(in_4), .clk(in_5), .ld(in_3), .clr(in_6));

  // Other names for the same wires on the sheet: _0写1读 = in_3; 时钟 = in_5; 清零 = in_6; 片选 = in_4
endmodule

module \_8位寄存器  (
  input  in_1,
  input  in_2,
  input  [7:0] in_3,
  output [7:0] out_4
);

  D_Flip_Flop d_ff_1 (.clk(in_1), .D(in_3[0]), .Q(out_4[0]), .en(in_2));  // open: Qn, preset, reset
  D_Flip_Flop d_ff_2 (.clk(in_1), .D(in_3[1]), .Q(out_4[1]), .en(in_2));  // open: Qn, preset, reset
  D_Flip_Flop d_ff_3 (.clk(in_1), .D(in_3[2]), .Q(out_4[2]), .en(in_2));  // open: Qn, preset, reset
  D_Flip_Flop d_ff_4 (.clk(in_1), .D(in_3[3]), .Q(out_4[3]), .en(in_2));  // open: Qn, preset, reset
  D_Flip_Flop d_ff_5 (.clk(in_1), .D(in_3[4]), .Q(out_4[4]), .en(in_2));  // open: Qn, preset, reset
  D_Flip_Flop d_ff_6 (.clk(in_1), .D(in_3[5]), .Q(out_4[5]), .en(in_2));  // open: Qn, preset, reset
  D_Flip_Flop d_ff_7 (.clk(in_1), .D(in_3[6]), .Q(out_4[6]), .en(in_2));  // open: Qn, preset, reset
  D_Flip_Flop d_ff_8 (.clk(in_1), .D(in_3[7]), .Q(out_4[7]), .en(in_2));  // open: Qn, preset, reset

  // Other names for the same wires on the sheet: 使能 = in_2; 时钟 = in_1
endmodule

module \_16x8寄存器  (
  input  in_1,
  input  in_2,
  input  [3:0] in_3,
  input  [7:0] in_4,
  input  [3:0] in_5,
  input  [3:0] in_6,
  output [7:0] out_7,
  output [7:0] out_8,
  output [7:0] out_9,
  output [7:0] out_10
);

  wire \寄存器1使能 , \寄存器2使能 , \寄存器3使能 , \寄存器4使能 , \寄存器5使能 , \寄存器6使能 , \寄存器7使能 , \寄存器8使能 , \寄存器9使能 , \寄存器10使能 ,
       \寄存器11使能 , \寄存器12使能 , \寄存器13使能 , \寄存器14使能 , \寄存器15使能 , \寄存器16使能 ;
  wire [7:0] \_1输出 , \_2输出 , \_3输出 , \_4输出 , \_5输出 , \_6输出 , \_7输出 , \_8输出 , \_9输出 , \_10输出 , \_11输出 ,
       \_12输出 , \_13输出 , \_14输出 , \_15输出 , \_16输出 ;

  Decoder #(.select(4), .disabled(0)) decoder_1 (
    .out0(\寄存器1使能 ), .out1(\寄存器2使能 ), .out2(\寄存器3使能 ), .out3(\寄存器4使能 ), .out4(\寄存器5使能 ), .out5(\寄存器6使能 ),
    .out6(\寄存器7使能 ), .out7(\寄存器8使能 ), .out8(\寄存器9使能 ), .out9(\寄存器10使能 ), .out10(\寄存器11使能 ),
    .out11(\寄存器12使能 ), .out12(\寄存器13使能 ), .out13(\寄存器14使能 ), .out14(\寄存器15使能 ), .out15(\寄存器16使能 ),
    .sel(in_3), .en(in_2));
  \_8位寄存器  \u_8位寄存器_1  (.in_1(in_1), .in_2(\寄存器1使能 ), .in_3(in_4), .out_4(\_1输出 ));
  \_8位寄存器  \u_8位寄存器_2  (.in_1(in_1), .in_2(\寄存器5使能 ), .in_3(in_4), .out_4(\_5输出 ));
  \_8位寄存器  \u_8位寄存器_3  (.in_1(in_1), .in_2(\寄存器9使能 ), .in_3(in_4), .out_4(\_9输出 ));
  \_8位寄存器  \u_8位寄存器_4  (.in_1(in_1), .in_2(\寄存器13使能 ), .in_3(in_4), .out_4(\_13输出 ));
  \_8位寄存器  \u_8位寄存器_5  (.in_1(in_1), .in_2(\寄存器2使能 ), .in_3(in_4), .out_4(\_2输出 ));
  \_8位寄存器  \u_8位寄存器_6  (.in_1(in_1), .in_2(\寄存器6使能 ), .in_3(in_4), .out_4(\_6输出 ));
  \_8位寄存器  \u_8位寄存器_7  (.in_1(in_1), .in_2(\寄存器10使能 ), .in_3(in_4), .out_4(\_10输出 ));
  \_8位寄存器  \u_8位寄存器_8  (.in_1(in_1), .in_2(\寄存器14使能 ), .in_3(in_4), .out_4(\_14输出 ));
  Multiplexer #(.select(4), .width(8)) multiplexer_1 (
    .in0(\_1输出 ), .in1(\_2输出 ), .in2(\_3输出 ), .in3(\_4输出 ), .in4(\_5输出 ), .in5(\_6输出 ), .in6(\_7输出 ),
    .in7(\_8输出 ), .in8(\_9输出 ), .in9(\_10输出 ), .in10(\_11输出 ), .in11(\_12输出 ), .in12(\_13输出 ),
    .in13(\_14输出 ), .in14(\_15输出 ), .in15(\_16输出 ), .out(out_7), .sel(in_5), .en(in_2));
  Multiplexer #(.select(4), .width(8)) multiplexer_2 (
    .in0(\_1输出 ), .in1(\_2输出 ), .in2(\_3输出 ), .in3(\_4输出 ), .in4(\_5输出 ), .in5(\_6输出 ), .in6(\_7输出 ),
    .in7(\_8输出 ), .in8(\_9输出 ), .in9(\_10输出 ), .in10(\_11输出 ), .in11(\_12输出 ), .in12(\_13输出 ),
    .in13(\_14输出 ), .in14(\_15输出 ), .in15(\_16输出 ), .out(out_9), .sel(in_6), .en(in_2));
  \_8位寄存器  \u_8位寄存器_9  (.in_1(in_1), .in_2(\寄存器3使能 ), .in_3(in_4), .out_4(\_3输出 ));
  \_8位寄存器  \u_8位寄存器_10  (.in_1(in_1), .in_2(\寄存器7使能 ), .in_3(in_4), .out_4(\_7输出 ));
  \_8位寄存器  \u_8位寄存器_11  (.in_1(in_1), .in_2(\寄存器11使能 ), .in_3(in_4), .out_4(\_11输出 ));
  \_8位寄存器  \u_8位寄存器_12  (.in_1(in_1), .in_2(\寄存器15使能 ), .in_3(in_4), .out_4(\_15输出 ));
  \_8位寄存器  \u_8位寄存器_13  (.in_1(in_1), .in_2(\寄存器4使能 ), .in_3(in_4), .out_4(\_4输出 ));
  \_8位寄存器  \u_8位寄存器_14  (.in_1(in_1), .in_2(\寄存器8使能 ), .in_3(in_4), .out_4(\_8输出 ));
  \_8位寄存器  \u_8位寄存器_15  (.in_1(in_1), .in_2(\寄存器12使能 ), .in_3(in_4), .out_4(\_12输出 ));
  \_8位寄存器  \u_8位寄存器_16  (.in_1(in_1), .in_2(\寄存器16使能 ), .in_3(in_4), .out_4(\_16输出 ));

  assign out_8 = out_7;
  assign out_10 = out_9;

  // Other names for the same wires on the sheet: 写地址[3:0] = in_3; 寄存器使能 = in_2; 数据输出1[7:0] = out_7;
  //   数据输出2[7:0] = out_9; 时钟 = in_1; 读地址1[3:0] = in_5; 读地址2[3:0] = in_6; 输入[7:0] = in_4
endmodule

module \程序计数控制器  (
  input  \时钟 ,
  input  \_1清零 ,
  input  [7:0] in_3,
  input  in_4,
  input  in_5,
  output [7:0] \指令地址 
);

  wire undriven;
  wire [7:0] register_1_q;

  Register register_1 (.D(\指令地址 ), .en(in_5), .Q(register_1_q), .clk(\时钟 ), .clr(\_1清零 ));
  \第二版运算单元  \u_第二版运算单元_1  (
    .in_1(undriven), .in_2(register_1_q), .in_3(in_3), .in_4(in_4), .in_5(in_5), .out_6(\指令地址 ));  // open: out_7
endmodule

module \第3版CPU  (
  input  \不加有时序错误 ,
  input  [7:0] in_2,
  input  in_3,
  input  in_4,
  input  in_5,
  output [3:0] out_6,
  output [3:0] out_7,
  output [3:0] out_8,
  output [3:0] out_9,
  output [7:0] out_10,
  output [3:0] out_11,
  output [3:0] out_12,
  output [3:0] out_13
);

  wire \_0加法1减法 , and_1_out, \n0检测器_1_out_2 , not_1_out, or_1_out, or_2_out, \加法指令 , \加载指令 , \存储器使能 , \存储指令 ,
       \时钟 , \立即数指令 , \跳转指令 , \运算单元使能 ;
  wire [7:0] multiplexer_1_out, \Rd数据 , register_1_q, \Rs1数据 , \Rs2数据 , \程序地址 ;

  \_0检测器  \u_0检测器_1  (.in_1(\Rs1数据 ), .out_2(\n0检测器_1_out_2 ));
  Clock #(.highDuration(5), .lowDuration(5)) clock_1 (.out(\时钟 ));
  Multiplexer #(.width(8), .enable("false")) multiplexer_1 (
    .in0(in_2), .in1(out_10), .out(multiplexer_1_out), .sel(and_1_out));
  and and_1 (and_1_out, \跳转指令 , \n0检测器_1_out_2 );
  Register register_1 (.D(multiplexer_1_out), .en(1'b1), .Q(register_1_q), .clk(\时钟 ));  // open: clr
  RAM #(.bus("separate")) ram_1 (
    .addr(out_10), .din(\Rs1数据 ), .data(\Rd数据 ), .str(\存储指令 ), .sel(\存储器使能 ), .clk(\时钟 ), .ld(\加载指令 ),
    .clr(in_5));
  \程序计数控制器  \u_程序计数控制器_1  (
    .\时钟 (\时钟 ), .in_3(register_1_q), .in_4(in_3), .in_5(1'b1), .\_1清零 (\不加有时序错误 ), .\指令地址 (\程序地址 ));
  RAM #(.dataWidth(16)) ram_2 (
    .addr(\程序地址 ), .data({out_9, out_8, out_6, out_13}), .sel(1'b1), .clk(\时钟 ), .ld(1'b1));  // open: clr
  Decoder #(.select(4), .disabled(0), .enable("false")) decoder_1 (
    .out0(\立即数指令 ), .out1(\加法指令 ), .out2(\_0加法1减法 ), .out3(\加载指令 ), .out4(\存储指令 ), .out5(\跳转指令 ), .sel(out_9));  // open: out6, out7, out8, out9, out10, out11, out12, out13, out14, out15
  or or_1 (or_1_out, \存储指令 , \跳转指令 );
  Multiplexer #(.width(4), .enable("false")) multiplexer_2 (.in0(out_6), .in1(out_8), .out(out_7), .sel(or_1_out));
  or or_2 (or_2_out, \立即数指令 , \加载指令 , \跳转指令 , \存储指令 );
  or or_3 (\运算单元使能 , \加法指令 , \_0加法1减法 );
  assign out_10 = or_2_out ? {out_6, out_13} : 8'bz;  // Controlled_Buffer controlled_buffer_1
  assign \Rd数据  = not_1_out ? out_10 : 8'bz;  // Controlled_Buffer controlled_buffer_2
  not not_1 (not_1_out, \加载指令 );
  or or_4 (\存储器使能 , \加载指令 , \存储指令 );
  \_16x8寄存器  \u_16x8寄存器_1  (
    .in_1(\时钟 ), .in_2(1'b1), .in_3(out_8), .in_4(\Rd数据 ), .in_5(out_7), .in_6(out_13), .out_8(\Rs1数据 ),
    .out_9(\Rs2数据 ));  // open: out_7, out_10
  \第二版运算单元  \u_第二版运算单元_1  (
    .in_1(in_4), .in_2(\Rs1数据 ), .in_3(\Rs2数据 ), .in_4(\_0加法1减法 ), .in_5(\运算单元使能 ), .out_6(\Rd数据 ));  // open: out_7

  assign out_11 = out_8;
  assign out_12 = out_6;

  // Other names for the same wires on the sheet: Rs2[3:0] = out_13; 指令[15:0] = {out_9, out_8, out_6, out_13};
  //   Rs1[3:0] = out_6; A[7:0] = out_10; 减法指令 = \_0加法1减法 ; Rd[3:0] = out_8; 操作码[3:0] = out_9

  // Notes on the sheet:
  //   记得设置为1
  //   指令译码
  //   数据存储器
  //   指令控制器
  //   logisim中存储器按字编址
  //   指令见指令结构
  //   指令控制
  //   寄存器
  //   运算单元
endmodule

module \_0检测器  (
  input  [7:0] in_1,
  output out_2
);

  nor nor_1 (out_2, in_1[0], in_1[1], in_1[2], in_1[3], in_1[4], in_1[5], in_1[6], in_1[7]);
endmodule
